# Fritzing sketch 模块接线图 (saved by Fritzing 0.9.3b)

parts:
  U1 = ESP32S-HiLetgo [part_number=ESP32S-HiLetgo]
  元件2 = Motor Driver 1A Dual TB6612FNG
  DC_Mot_Enc1 = DC Motor with two-phase hall-encoder [part_number=VT-E-G25A-06-177E]
  DC_Mot_Enc2 = DC Motor with two-phase hall-encoder [part_number=VT-E-G25A-06-177E]
  GY1 = MPU-6050 Board GY-521 [form="♀ (female)" package=THT]

nets:
  N1: U1.GPIO33, DC_Mot_Enc1.pin3
  N2: U1.GPIO27, DC_Mot_Enc2.pin3
  N3: U1.GPIO14, DC_Mot_Enc2.pin4
  N4: U1.GND, GY1.pin2
  N5: U1.GPIO13, DC_Mot_Enc1.pin4
  N6: U1.VIN, 元件2.VM, DC_Mot_Enc1.pin5, DC_Mot_Enc2.pin5, GY1.pin1
  N7: U1.GPIO6, 元件2.GND, DC_Mot_Enc1.pin2, DC_Mot_Enc2.pin2
  N8: U1.GPIO15, 元件2.PWMA
  N9: U1.GPIO2, 元件2.AIN2
  N10: U1.GPIO0, 元件2.AIN1
  N11: U1.GPIO4, 元件2.STBY
  N12: U1.GPIO16, 元件2.BIN1
  N13: U1.GPIO17, 元件2.BIN2
  N14: U1.GPIO5, 元件2.PWMB
  N15: U1.GPIO21, GY1.pin4
  N16: U1.GPIO22, GY1.pin3
  N17: 元件2.B01, DC_Mot_Enc1.pin1
  N18: 元件2.B02, DC_Mot_Enc1.pin6
  N19: 元件2.A02, DC_Mot_Enc2.pin1
  N20: 元件2.A01, DC_Mot_Enc2.pin6

custom parts:
  ESP32S-HiLetgo: HiLetgo ESP-WROOM-32 ESP32 ESP-32S Development Board 2.4GHz Dual-Mode WiFi + Bluetooth Dual Cores Microcontroller The ESP32 integrated with Antenna switches, RF Balun, power amplifiers, low-noise amplifiers, filters, and management modules, and the entire solution occupies the least area of PCB. 2.4 GHz Wi-Fi plus Bluetooth dual-mode chip, with TSMC Ultra-low power consumption 40nm technology,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
  MPU-6050 Board GY-521: Acelerometro y Giroscopio MPU-6050 Board GY-521
